# Fritzing sketch MidTerm board (saved by Fritzing 1.0.4)
breadboards: 1

parts:
  OLED_I2C1 = OLED 128x64 I2C Monochrome Display
  A1 = Particle - Photon2
  Part1 = Adafruit MAX4466 Electret Microphone Amplifier [part_number="Adafruit #1063"]
  Neopixel1 = Adafruit RBG Smart Neopixel [package="DIP (Dual Inline) [THT]"]
  Neopixel2 = Adafruit RBG Smart Neopixel [package="DIP (Dual Inline) [THT]"]
  Neopixel3 = Adafruit RBG Smart Neopixel [package="DIP (Dual Inline) [THT]"]
  Part2 = 16 NeoPixel Ring [part_number=1463]
  S1 = Momentary Switch [package=ksa_sealed_tac_switch]
  S2 = Momentary Switch [package=ksa_sealed_tac_switch]
  LED1 = smd LED [color="Yellow (595nm)" package="0805 [SMD]"]
  S3 = SPST Switch [package=switche-dpdt]

nets:
  N1: OLED_I2C1.SDA, S2.3
  N2: OLED_I2C1.VDD, LED1.anode
  GND: OLED_I2C1.GND, Part1.GND, Neopixel1.G, Neopixel2.G, Neopixel3.G, Part2.GND, S1.2, S2.2
  N3: A1.Pin_30, A1.Pin_35, S3.O
  VCC: Part1.VCC, Neopixel1.+, Neopixel2.+, Neopixel3.+, Part2.VDD
  N4: Neopixel1.O, Neopixel2.In
  N5: Neopixel2.O, Neopixel3.In
  N6: Neopixel3.O, Part2.IN

custom parts:
  Particle - Photon2: The Photon 2 is a microcontroller and Wi-Fi networking developed by particle. Features: 802.11a/b/g/n Wi-Fi, 2.4 GHz and 5 GHz Integrated PCB antenna Integrated U.FL connector for external antenna Integrated RF switch BLE 5 using same antenna as Wi-Fi Realtek RTL8721DM MCU ARM Cortex M33 CPU, 200 MHz 2048 KB (2 MB) user application maximum size 3072 KB (3 MB) of RAM available to user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
  Adafruit MAX4466 Electret Microphone Amplifier: Add an ear to your project with this well-designed electret microphone amplifier. This fully assembled and tested board comes with a 20-20KHz electret microphone soldered on. For the amplification, we use the Maxim MAX4466, an op-amp specifically designed for this delicate task! The amplifier has excellent power supply noise rejection, so this amplifier sounds really good and isn't nearly as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
  16 NeoPixel Ring: 16 ultra bright smart LED NeoPixels are arranged in a circle with 1.75" (44.5mm) outer diameter. The rings are 'chainable' - connect the output pin of one to the input pin of another. Use only one microcontroller pin to control as many as you can chain together! Each LED is addressable as the driver chip is inside the LED. Each one has ~18mA constant current drive so the color will be very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
